# Fritzing sketch Schematic (saved by Fritzing 0.9.3b)
breadboards: 1

parts:
  Part1 = Arduino Uno (Rev3)
  IC1 = L293D [package=THT]
  IC2 = L293D [package=THT]
  M1 = DC Motor
  M2 = DC Motor
  M3 = DC Motor
  M4 = DC Motor
  VCC1 = Battery block 9V

nets:
  N1: Part1.D8, IC1.In_2
  N2: Part1.D9_PWM, IC1.In_1
  N3: Part1.D10_PWM/SS, IC1.Enable_1
  N4: Part1.D11_PWM/MOSI, IC1.Enable_2
  N5: Part1.D12/MISO, IC1.In_3
  N6: Part1.D13/SCK, IC1.In_4
  N7: Part1.GND, IC1.0V, IC2.0V, VCC1.-
  N8: Part1.D2, IC2.Enable_2
  N9: Part1.D3_PWM, IC2.In_3
  N10: Part1.D4, IC2.In_4
  N11: Part1.D5_PWM, IC2.Enable_1
  N12: Part1.D6_PWM, IC2.In_1
  N13: Part1.D7, IC2.In_2
  N14: Part1.5V, IC1.+V, IC2.+V
  N15: IC1.Out_1_(_Controlled_by_Enable_1_), M1.pin_2
  N16: IC1.Out_2_(_Controlled_by_Enable_1_), M1.pin_1
  N17: IC1.+Vmotor, IC2.+Vmotor, VCC1.+
  N18: IC1.Out_3_(_Controlled_by_Enable_2_), M2.pin_1
  N19: IC1.Out_4_(_Controlled_by_Enable_2_), M2.pin_2
  N20: IC2.Out_1_(_Controlled_by_Enable_1_), M4.pin_2
  N21: IC2.Out_2_(_Controlled_by_Enable_1_), M4.pin_1
  N22: IC2.Out_3_(_Controlled_by_Enable_2_), M3.pin_1
  N23: IC2.Out_4_(_Controlled_by_Enable_2_), M3.pin_2

notes:
  Rear Wheels
  Front Wheels
